# Fritzing sketch Line-Sensor-Erweiterung (saved by Fritzing 0.9.2b)

parts:
  Bauteil1 = Arduino Uno (Rev3)  # not connected
  Bauteil2 = Arduino Motor Shield (Rev3)
  M1 = DC Motor
  M2 = DC Motor
  VCC1 = 4 x AAA Battery Mount
  J1 = female pin header, 5 pins [form="♀ (female)"]

nets:
  N1: Bauteil2.A0, J1.pin3
  N2: Bauteil2.A1, J1.pin4
  N3: Bauteil2.A2, J1.pin5
  N4: Bauteil2.B-, M1.pin_2
  N5: Bauteil2.B+, M1.pin_1
  N6: Bauteil2.A-, M2.pin_2
  N7: Bauteil2.A+, M2.pin_1
  N8: Bauteil2.VMOT, VCC1.+
  N9: Bauteil2.GND, VCC1.-, J1.pin1
  N10: Bauteil2.5V, J1.pin2

notes:
  Pololu QTR-3A
